# Fritzing sketch LED (saved by Fritzing 0.9.2b)

parts:
  Raspberry_Pi1 = Raspberry Pi 2
  LED1 = smd LED [color="Red (633nm)" package="0603 [SMD]"]
  R1 = Resistor [tolerance=±5% resistance=220 package="2512 [SMD]"]

nets:
  3V3: Raspberry_Pi1.3v3, Raspberry_Pi1.3V3, R1.Pin_1
  N1: Raspberry_Pi1.GPIO6, LED1.cathode
  N2: LED1.anode, R1.Pin_0
